// Digital circuit Lab1 Schematic.dig as structural Verilog
module Lab1_Schematic (
  input  D,
  input  C,
  input  B,
  input  A,
  output Y
);

  wire _7404_1_pin9, _7404_1_pin11, _74151_1_pin12, notconnected_1_out, notconnected_2_out,
       notconnected_3_out;

  _74151 _74151_1 (
    .pin1(D), .pin2(D), .pin3(D), .pin4(D), .pin5(Y), .pin7(1'b0), .pin8(1'b0), .pin9(C), .pin10(B),
    .pin11(A), .pin12(_74151_1_pin12), .pin13(_74151_1_pin12), .pin14(_74151_1_pin12),
    .pin15(_74151_1_pin12), .pin16(1'b1));  // open: pin6
  // NotConnected on notconnected_1_out
  // NotConnected on notconnected_2_out
  // NotConnected on notconnected_3_out
  _7404 _7404_1 (
    .pin1(notconnected_1_out), .pin3(notconnected_2_out), .pin5(notconnected_3_out), .pin7(1'b0),
    .pin9(_7404_1_pin9), .pin11(_7404_1_pin11), .pin12(_74151_1_pin12), .pin13(D), .pin14(1'b1));  // open: pin2, pin4, pin6, pin8, pin10
  // NotConnected on _7404_1_pin11
  // NotConnected on _7404_1_pin9
endmodule

/* Test case:
D A B C Y
0 0 0 0 0
0 0 0 1 1
0 0 1 0 0
0 0 1 1 1
0 1 0 0 0
0 1 0 1 1
0 1 1 0 0
0 1 1 1 1
1 0 0 0 1
1 0 0 1 0 
1 0 1 0 1
1 0 1 1 0
1 1 0 0 1
1 1 0 1 0
1 1 1 0 1
1 1 1 1 0
*/
